// Logisim project draw-1.circ as structural Verilog: 1 circuit, main circuit main
module main (
);

  wire undriven_2;
  wire [3:0] undriven_3;
  wire [9:0] demultiplexer_1_out13, input_buffer_of_one_triac_driver_q, undriven;

  Demultiplexer #(.select(4), .width(10)) demultiplexer_1 (
    .out13(demultiplexer_1_out13), .in(undriven), .sel(undriven_3), .en(undriven_2));  // open: out0, out1, out2, out3, out4, out5, out6, out7, out8, out9, out10, out11, out12, out14, out15
  Register #(.width(10)) input_buffer_of_one_triac_driver (
    .D(demultiplexer_1_out13), .Q(input_buffer_of_one_triac_driver_q));  // open: en, clk, clr

  // Notes on the sheet:
  //   input data [0..10]
  //   input strobe (data, address ready)
  //   input address [0..n]
  //   enable
endmodule
